# Fritzing sketch grid-homekitrgb-1 (saved by Fritzing 0.9.3b)
breadboards: 1

parts:
  12V-5V = RioRand LM2596
  NodeMCU_ESP8266_ESP12-E = Gizwits WiFi Witty ESP-12F
  Q1 = NPN-Transistor [package="TO92 [THT]"]
  12V_In = Power plug
  Q2 = NPN-Transistor [package="TO92 [THT]"]
  Q3 = NPN-Transistor [package="TO92 [THT]"]
  SMD5050 = RGB LED (com. cathode, rbg) [package="5 mm [THT]"]

nets:
  N1: 12V-5V.Pin_1, 12V_In.VCC, SMD5050.common_cathode
  N2: 12V-5V.Pin_2, Q1.E, 12V_In.GND, Q2.E, Q3.E
  N3: 12V-5V.Pin_3, NodeMCU_ESP8266_ESP12-E.VCC
  N4: 12V-5V.Pin_4, NodeMCU_ESP8266_ESP12-E.GND
  N5: NodeMCU_ESP8266_ESP12-E.GPIO2, Q3.B
  N6: NodeMCU_ESP8266_ESP12-E.GPIO0, Q2.B
  N7: NodeMCU_ESP8266_ESP12-E.GPIO4, Q1.B
  N8: Q1.C, SMD5050.red_anode
  N9: Q2.C, SMD5050.blue_anode
  N10: Q3.C, SMD5050.green_anode
